// Digital circuit 1-bit-adder-2.dig as structural Verilog
module _1_bit_adder_2 (
  input  A,
  input  B,
  input  C_in,
  output Sum,
  output C_out
);

  wire and_1_out, and_2_out, and_3_out, and_4_out, and_5_out, and_6_out, and_7_out, not_1_out, not_2_out,
       not_3_out, not_4_out;

  not not_1 (not_1_out, A);
  not not_2 (not_2_out, B);
  not not_3 (not_3_out, A);
  not not_4 (not_4_out, B);
  and and_1 (and_1_out, not_1_out, not_2_out, C_in);
  and and_2 (and_2_out, not_3_out, B, C_in);
  and and_3 (and_3_out, A, not_4_out, C_in);
  and and_4 (and_4_out, A, B, C_in);
  or or_1 (Sum, and_1_out, and_2_out, and_3_out, and_4_out);
  and and_5 (and_5_out, B, C_in);
  and and_6 (and_6_out, A, B);
  and and_7 (and_7_out, A, C_in);
  or or_2 (C_out, and_5_out, and_6_out, and_7_out);
endmodule
