// Digital circuit 2-bit-Multiplier.dig as structural Verilog
module _2_bit_Multiplier (
  input  [1:0] A,
  input  [1:0] B,
  output [3:0] Output
);

  wire and_1_out, and_2_out, and_3_out, and_4_out, and_5_out, and_6_out, not_1_out, not_2_out, not_3_out,
       not_4_out, not_5_out, not_6_out;

  not not_1 (not_1_out, A[0]);
  not not_2 (not_2_out, B[0]);
  and and_1 (and_1_out, A[1], not_1_out, B[1]);
  and and_2 (and_2_out, A[1], B[1], not_2_out);
  or or_1 (Output[2], and_1_out, and_2_out);
  not not_3 (not_3_out, A[0]);
  not not_4 (not_4_out, B[1]);
  and and_3 (and_3_out, A[1], not_3_out, B[0]);
  not not_5 (not_5_out, B[0]);
  not not_6 (not_6_out, A[1]);
  and and_4 (and_4_out, A[1], not_4_out, B[0]);
  and and_5 (and_5_out, A[0], B[1], not_5_out);
  and and_6 (and_6_out, not_6_out, A[0], B[1]);
  or or_2 (Output[1], and_4_out, and_3_out, and_5_out, and_6_out);
  and and_7 (Output[0], A[0], B[0]);
  and and_8 (Output[3], A[0], A[1], B[0], B[1]);
endmodule
