// Digital circuit 4-bit-adder.dig as structural Verilog
module _4_bit_adder (
  input  [3:0] A,
  input  [3:0] B,
  output [3:0] Sum,
  output Overflow_flag
);

  wire _1_bit_adder_1_p3, _1_bit_adder_2_p3, _1_bit_adder_3_p3;

  // _1_bit_adder _1_bit_adder_1: pin names not known; wires that end beside it: A[3], B[3], _1_bit_adder_1_p3, Sum[3], Overflow_flag
  // _1_bit_adder _1_bit_adder_2: pin names not known; wires that end beside it: A[2], B[2], _1_bit_adder_2_p3, Sum[2], _1_bit_adder_1_p3
  // _1_bit_adder _1_bit_adder_3: pin names not known; wires that end beside it: A[1], B[1], _1_bit_adder_3_p3, Sum[1], _1_bit_adder_2_p3
  // _1_bit_adder _1_bit_adder_4: pin names not known; wires that end beside it: A[0], B[0], 1'b0, Sum[0], _1_bit_adder_3_p3
endmodule
